// Logisim project division.circ as structural Verilog: 1 circuit, main circuit main
module main (
  input  [7:0] dividendo,
  input  [3:0] divisor,
  output [3:0] out_3,
  output [3:0] out_4
);

  wire [3:0] divisoriter_1_cocienteout, divisoriter_1_divisorout, divisoriter_1_residuoout,
       divisoriter_2_cocienteout, divisoriter_2_divisorout, divisoriter_2_residuoout,
       divisoriter_3_cocienteout, divisoriter_3_divisorout, divisoriter_3_residuoout,
       divisoriter_4_cocienteout, divisoriter_4_divisorout, divisoriter_4_residuoout,
       divisoriter_5_cocienteout, divisoriter_5_divisorout, divisoriter_5_residuoout,
       divisoriter_6_cocienteout, divisoriter_6_divisorout, divisoriter_6_residuoout,
       divisoriter_7_cocienteout, divisoriter_7_divisorout, divisoriter_7_residuoout;
  wire [7:0] divisoriter_1_dividendoout, divisoriter_2_dividendoout, divisoriter_3_dividendoout,
       divisoriter_4_dividendoout, divisoriter_5_dividendoout, divisoriter_6_dividendoout,
       divisoriter_7_dividendoout;

  divisorIter divisoriter_1 (
    .dividendo(dividendo), .divisor(divisor), .cociente(4'b0000), .residuo(4'b0000),
    .dividendoOut(divisoriter_1_dividendoout), .divisorOut(divisoriter_1_divisorout),
    .cocienteOut(divisoriter_1_cocienteout), .residuoOut(divisoriter_1_residuoout));
  divisorIter divisoriter_2 (
    .dividendo(divisoriter_1_dividendoout), .divisor(divisoriter_1_divisorout),
    .cociente(divisoriter_1_cocienteout), .residuo(divisoriter_1_residuoout),
    .dividendoOut(divisoriter_2_dividendoout), .divisorOut(divisoriter_2_divisorout),
    .cocienteOut(divisoriter_2_cocienteout), .residuoOut(divisoriter_2_residuoout));
  divisorIter divisoriter_3 (
    .dividendo(divisoriter_2_dividendoout), .divisor(divisoriter_2_divisorout),
    .cociente(divisoriter_2_cocienteout), .residuo(divisoriter_2_residuoout),
    .dividendoOut(divisoriter_3_dividendoout), .divisorOut(divisoriter_3_divisorout),
    .cocienteOut(divisoriter_3_cocienteout), .residuoOut(divisoriter_3_residuoout));
  divisorIter divisoriter_4 (
    .dividendo(divisoriter_3_dividendoout), .divisor(divisoriter_3_divisorout),
    .cociente(divisoriter_3_cocienteout), .residuo(divisoriter_3_residuoout),
    .dividendoOut(divisoriter_4_dividendoout), .divisorOut(divisoriter_4_divisorout),
    .cocienteOut(divisoriter_4_cocienteout), .residuoOut(divisoriter_4_residuoout));
  divisorIter divisoriter_5 (
    .dividendo(divisoriter_4_dividendoout), .divisor(divisoriter_4_divisorout),
    .cociente(divisoriter_4_cocienteout), .residuo(divisoriter_4_residuoout),
    .dividendoOut(divisoriter_5_dividendoout), .divisorOut(divisoriter_5_divisorout),
    .cocienteOut(divisoriter_5_cocienteout), .residuoOut(divisoriter_5_residuoout));
  divisorIter divisoriter_6 (
    .dividendo(divisoriter_5_dividendoout), .divisor(divisoriter_5_divisorout),
    .cociente(divisoriter_5_cocienteout), .residuo(divisoriter_5_residuoout),
    .dividendoOut(divisoriter_6_dividendoout), .divisorOut(divisoriter_6_divisorout),
    .cocienteOut(divisoriter_6_cocienteout), .residuoOut(divisoriter_6_residuoout));
  divisorIter divisoriter_7 (
    .dividendo(divisoriter_6_dividendoout), .divisor(divisoriter_6_divisorout),
    .cociente(divisoriter_6_cocienteout), .residuo(divisoriter_6_residuoout),
    .dividendoOut(divisoriter_7_dividendoout), .divisorOut(divisoriter_7_divisorout),
    .cocienteOut(divisoriter_7_cocienteout), .residuoOut(divisoriter_7_residuoout));
  divisorIter divisoriter_8 (
    .dividendo(divisoriter_7_dividendoout), .divisor(divisoriter_7_divisorout),
    .cociente(divisoriter_7_cocienteout), .residuo(divisoriter_7_residuoout), .cocienteOut(out_3),
    .residuoOut(out_4));  // open: dividendoOut, divisorOut

  // Other names for the same wires on the sheet: cociente[3:0] = out_3; residuo[3:0] = out_4
endmodule
