// Logisim project divisorIteracion.circ as structural Verilog: 1 circuit, main circuit divisorIter
module divisorIter (
  input  [15:0] dividendo,
  input  [7:0] divisor,
  input  [7:0] cociente,
  input  [7:0] residuo,
  output [15:0] dividendoOut,
  output [7:0] divisorOut,
  output [7:0] cocienteOut,
  output [7:0] residuoOut
);

  wire comparator_1_lt;
  wire [7:0] multiplexer_1_out, subtractor_1_out;

  Multiplexer #(.width(8)) multiplexer_1 (
    .in0({residuo[6:0], 1'b0}), .in1({residuo[6:0], 1'b1}), .out(multiplexer_1_out), .sel(dividendo[15]));
  Comparator #(.mode("unsigned")) comparator_1 (
    .a(multiplexer_1_out), .b(divisor), .lt(comparator_1_lt));  // open: gt, eq
  Subtractor subtractor_1 (.a(multiplexer_1_out), .b(divisor), .out(subtractor_1_out));  // open: bin, bout
  Multiplexer #(.width(8)) multiplexer_2 (
    .in0({cociente[6:0], 1'b1}), .in1({cociente[6:0], 1'b0}), .out(cocienteOut), .sel(comparator_1_lt));
  Multiplexer #(.width(8)) multiplexer_3 (
    .in0(subtractor_1_out), .in1(multiplexer_1_out), .out(residuoOut), .sel(comparator_1_lt));

  assign dividendoOut = {dividendo[14:0], 1'b0};
  assign divisorOut = divisor;
endmodule
